// Logisim project MIPS.circ as structural Verilog
module MIPS (
  input  [31:0] in_1
);

  wire mipsprogramrom_1_p1, registerfile_1_p1, registerfile_1_p2;

  // Incrementer incrementer_1: pin names not known
  // Mips_ALU mips_alu_1: pin names not known; wires that end beside it: in_1
  // Mips_ALU mips_alu_2: pin names not known
  // MIPSProgramROM mipsprogramrom_1: pin names not known; wires that end beside it: mipsprogramrom_1_p1, mipsprogramrom_1_p1
  Multiplexer multiplexer_1 ();  // open: in0, in1, out, sel, en
  // LCD_Video lcd_video_1: pin names not known
  // MIPS_RAM mips_ram_1: pin names not known
  // RegisterFile registerfile_1: pin names not known; wires that end beside it: registerfile_1_p1, registerfile_1_p2, registerfile_1_p1, registerfile_1_p2
endmodule

module Fetch (
  input  [31:0] in_1,
  output [31:0] out_2
);

  // MIPS_RAM mips_ram_1: pin names not known
  // RegisterFile registerfile_1: pin names not known
  // MIPSProgramROM mipsprogramrom_1: pin names not known; wires that end beside it: in_1, out_2
endmodule
